# Fritzing sketch Receiver connection ESP32 (saved by Fritzing 0.9.5d)

parts:
  Componente1 = Arduino Uno (Rev3) - ICSP
  U1 = lolin

nets:
  N1: Componente1.A0, U1.connector11
  N2: Componente1.A1, U1.connector10
  N3: Componente1.A2, U1.connector9
  N4: Componente1.A3, U1.connector8
  N5: Componente1.GND, U1.connector15
