# Fritzing sketch Receiver connection ESP8266 (saved by Fritzing 0.9.5d)

parts:
  Componente1 = Arduino Uno (Rev3) - ICSP
  WeMos_D1_Mini1 = WeMos D1 Mini

nets:
  N1: Componente1.A0, WeMos_D1_Mini1.D8
  N2: Componente1.A1, WeMos_D1_Mini1.D7
  N3: Componente1.A2, WeMos_D1_Mini1.D6
  N4: Componente1.A3, WeMos_D1_Mini1.D5
  N5: Componente1.GND, WeMos_D1_Mini1.G
